# Fritzing sketch circuit (saved by Fritzing 0.9.3b)
breadboards: 1

parts:
  U2 = ESP-WROOM-02-AE [part_number=ESP-WROOM-02-AE]
  IC1 = IC, DIP package, 28 pins [chip_label=ATP3011F4-PU]
  C1 = Electrolytic Capacitor [capacitance=47µF voltage=50V package="100 mil [THT, electrolytic]"]
  C2 = Ceramic Capacitor [capacitance=470nF package="100 mil [THT, multilayer]"]
  S1 = Pushbutton [package=THT]
  R1 = Resistor [tolerance=±5% resistance=10k package=THT]
  LED1 = LED - 5mm [color="Red (633nm)" package="5 mm [THT]"]
  R2 = Resistor [tolerance=±5% resistance=470 package=THT]
  C3 = Ceramic Capacitor [capacitance=100nF package="100 mil [THT, multilayer]"]
  R3 = Resistor [tolerance=±5% resistance=1k package=THT]
  R4 = Resistor [tolerance=±5% resistance=3.3k package=THT]
  SPKR1 = Loudspeaker
  Q1 = NPN-Transistor [package="TO92 [THT]"]
  IC2 = IC, SIP package, 3 pins [chip_label=72233J]
  J1 = female pin header, 2 pins [form="♀ (female)"]

nets (from the schematic view):
  N1: U2.3V3, U2.EN, U2.IO0, IC1.pin4, IC1.pin5, IC1.pin7, IC1.pin14, IC1.pin15, C2.1, R1.Pin_1, C3.1, R3.Pin_1, SPKR1.pin1, IC2.pin1
  N2: U2.IO14, IC1.pin1
  N3: U2.IO15, U2.GND, IC1.pin8, C1.-, C2.0, S1.leg1, R2.Pin_0, C3.0, Q1.E, IC2.pin3, J1.pin1
  N4: U2.IO2, IC1.pin2, R3.Pin_0
  N5: U2.RST, S1.leg0, R1.Pin_0
  N6: U2.IO5, LED1.anode
  N7: IC1.pin12, R4.Pin_1
  N8: C1.+, IC2.pin2, J1.pin2
  N9: LED1.cathode, R2.Pin_1
  N10: R4.Pin_0, Q1.B
  N11: SPKR1.pin2, Q1.C

custom parts:
  ESP-WROOM-02-AE: ESP-WROOM-02 with the DIP breakout board by Akizuki-Electronics in Japan. See http://akizukidenshi.com/catalog/g/gK-09758/ for the detauls.
